# Fritzing sketch PartyBot (saved by Fritzing 0.9.3b)
breadboards: 1

parts:
  Part1 = Arduino Uno (Rev3) - ICSP
  PIR1 = PIR sensor
  R1 = Resistor [tolerance=±5% resistance=10k package="0805 [SMD]"]

nets:
  N1: Part1.D4, PIR1.SIG, R1.Pin_0
  5V: Part1.5V, PIR1.VDD, R1.Pin_1
  GND: Part1.GND, PIR1.GND
