# Fritzing sketch WeatherBot (saved by Fritzing 0.9.3b)
breadboards: 1

parts:
  Part1 = Adafruit Feather HUZZAH ESP8266 [part_number="Adafruit #2821"]
  Part2 = Adafruit Quad AlphaNumeric Featherwing - Yellow-Green [part_number="Adafruit #3132"]
  Part3 = Arduino Uno (Rev3) - ICSP
  DHT1 = DHT22 Humidity and Temperature Sensor
  R1 = Resistor [tolerance=±5% resistance=10k package="0805 [SMD]"]

nets:
  N1: Part1.CH_PD, Part2.G
  N2: Part1.TXD, Part2.TX
  N3: Part1.RXD, Part2.RX
  N4: Part1.GPIO12/MISO, Part2.SCK, Part3.D4, DHT1.DATA, R1.Pin_1
  N5: Part1.GPIO13/MOSI, Part2.L, Part2.MISO
  N6: Part1.GPIO14/SCK, Part2.MOSI
  N7: Part1.ADC, Part2.A
  GND: Part1.GND, Part2.GND, Part3.GND, DHT1.GND
  3.3V: Part1.3.3V, Part2.VDD
  N8: Part1.RESET, Part2.RESET
  5V: Part1.VBAT, Part2.VBAT, Part3.5V, DHT1.VDD, R1.Pin_0
  N9: Part1.EN, Part2.EN
  N10: Part1.VBUS, Part2.USB
  N11: Part1.GPIO15, Part2.K
  N12: Part1.GPIO0, Part2.J
  N13: Part1.GPIO16, Part2.I
  N14: Part1.GPIO2, Part2.H
  N15: Part1.GPIO5/SCL, Part2.SCL
  N16: Part1.GPIO4/SDA, Part2.SDA

custom parts:
  Adafruit Feather HUZZAH ESP8266: his is the Adafruit Feather HUZZAH ESP8266 - our take on an 'all-in-one' ESP8266 WiFi development board with built in USB and battery charging. Its an ESP8266 WiFi module with all the extras you need, ready to rock! We have other boards in the Feather family, check'em out here. At the Feather HUZZAH's heart is an ESP8266 WiFi microcontroller clocked at 80 MHz and at 3.3V logic. This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
  Adafruit Quad AlphaNumeric Featherwing - Yellow-Green: This is the Yellow-Green Adafruit 0.54" Dual Alphanumeric Display w/ FeatherWing Combo Pack! We also have these combo packs in Green, White, Red, Blue, and Yellow. This is a nice, bright alphanumeric display that shows letters and numbers in a beautiful hue. It's super bright and designed for viewing from distances up to 23 feet (7 meters) away. Each of the digit sets have 14 segments on a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
